// Logisim project CPU.circ as structural Verilog: 9 circuits, main circuit main
module main (
  input  in_1,
  input  in_2,
  input  in_3,
  input  in_4,
  input  in_5,
  input  in_6,
  input  in_7,
  input  in_8
);
endmodule

module halfadder (
  input  A,
  input  B,
  output SUM,
  output CARRY
);

  xor xor_1 (SUM, A, B);
  and and_1 (CARRY, A, B);
endmodule

module fulladder (
  input  CIN,
  input  A,
  input  B,
  output Sum,
  output Carry
);

  wire and_1_out, and_2_out, xor_1_out;

  xor xor_1 (xor_1_out, A, B);
  and and_1 (and_1_out, A, B);
  xor xor_2 (Sum, xor_1_out, CIN);
  and and_2 (and_2_out, CIN, xor_1_out);
  or or_1 (Carry, and_2_out, and_1_out);
endmodule

module fourbitadder (
  input  in_1,
  input  A1,
  input  A3,
  input  B1,
  input  B3,
  input  A2,
  input  A4,
  input  B2,
  input  B4,
  output out_10,
  output out_11,
  output out_12,
  output out_13,
  output out_14
);

  wire fulladder_1_carry, fulladder_2_carry, fulladder_3_carry;

  fulladder fulladder_1 (.CIN(in_1), .A(A1), .B(A3), .Sum(out_10), .Carry(fulladder_1_carry));
  fulladder fulladder_2 (.CIN(fulladder_1_carry), .A(B1), .B(B3), .Sum(out_11), .Carry(fulladder_2_carry));
  fulladder fulladder_3 (.CIN(fulladder_2_carry), .A(A2), .B(A4), .Sum(out_12), .Carry(fulladder_3_carry));
  fulladder fulladder_4 (.CIN(fulladder_3_carry), .A(B2), .B(B4), .Sum(out_13), .Carry(out_14));
endmodule

module srlatch (
  input  S,
  input  R,
  output Q
);

  wire nor_2_out;

  nor nor_1 (Q, nor_2_out, R);
  nor nor_2 (nor_2_out, S, Q);
endmodule

module DLATCH (
  input  D,
  input  S,
  output Q
);

  wire and_1_out, and_2_out, nor_2_out, not_1_out;

  not not_1 (not_1_out, D);
  and and_1 (and_1_out, D, S);
  and and_2 (and_2_out, S, not_1_out);
  nor nor_1 (Q, nor_2_out, and_2_out);
  nor nor_2 (nor_2_out, and_1_out, Q);
endmodule

module DFLP (
  input  D,
  input  C,
  output Q
);

  wire dlatch_1_q, not_1_out;

  not not_1 (not_1_out, C);
  DLATCH dlatch_1 (.D(D), .S(not_1_out), .Q(dlatch_1_q));
  DLATCH dlatch_2 (.D(dlatch_1_q), .S(C), .Q(Q));
endmodule

module obreg (
  input  D,
  input  S,
  input  C,
  output out_4
);

  wire and_1_out, and_2_out, not_1_out, or_1_out;

  not not_1 (not_1_out, S);
  and and_1 (and_1_out, out_4, not_1_out);
  and and_2 (and_2_out, S, D);
  or or_1 (or_1_out, and_1_out, and_2_out);
  DFLP dflp_1 (.D(or_1_out), .C(C), .Q(out_4));
endmodule

module fourbitregister (
  input  I1,
  input  I2,
  input  I3,
  input  I4,
  input  S,
  input  C,
  output out_7,
  output out_8,
  output out_9,
  output out_10
);

  obreg obreg_1 (.D(I1), .S(S), .C(C), .out_4(out_7));
  obreg obreg_2 (.D(I2), .S(S), .C(C), .out_4(out_8));
  obreg obreg_3 (.D(I4), .S(S), .C(C), .out_4(out_10));
  obreg obreg_4 (.D(I3), .S(S), .C(C), .out_4(out_9));
endmodule
